# Fritzing sketch schema (saved by Fritzing 0.9.1b)
breadboards: 1

parts:
  Parte1 = Arduino Pro Mini v13
  J1 = Basic Servo
  R1 = Photocell (LDR) [package=THT]
  R2 = Resistor [tolerance=±5% resistance=220 package="0603 [SMD]"]

nets:
  GND: Parte1.GND, Parte1.RESET, J1.gnd, R2.Pin_1
  VCC: Parte1.VCC, J1.vcc, R1.pin_1
  N1: Parte1.A1, Parte1.A0, R1.pin_0, R2.Pin_0
  N2: Parte1.D9_PWM, J1.pulse
